// Digital circuit RegisterFile_ALU.dig as structural Verilog
module RegisterFile_ALU (
  input  Clock,
  input  [1:0] Read_Register1,
  input  [1:0] Read_Register2,
  input  [1:0] Write_Register,
  input  [7:0] Control,
  input  [2:0] Opcode,
  input  [7:0] Write_Data,
  input  Select
);

  wire [7:0] arithmetic_circuit_1_output, multiplexer_1_out, register_file_1_p7, register_file_1_p8;

  Multiplexer #(.Bits(8)) multiplexer_1 (
    .sel(Select), .in_0(Write_Data), .in_1(arithmetic_circuit_1_output), .out(multiplexer_1_out));
  // Register_File register_file_1: pin names not known; wires that end beside it: Clock, Read_Register1, Read_Register2, multiplexer_1_out, Control, Write_Register, register_file_1_p7, register_file_1_p8
  Arithmetic_Circuit arithmetic_circuit_1 (
    .A(register_file_1_p7), .S_1_S_0_C_in(Opcode), .B(register_file_1_p8),
    .Output(arithmetic_circuit_1_output));  // open: C_out
endmodule
